// Logisim project TallerLogica-Combinatorios.circ as structural Verilog: 9 circuits, main circuit verificador
module sumador_simple (
  input  A,
  input  B,
  output S,
  output Cout
);

  and and_1 (Cout, A, B);
  xor xor_1 (S, A, B);
endmodule

module sumador_completo (
  input  Cin,
  input  A,
  input  B,
  output S,
  output Cout
);

  wire sumador_simple_1_cout, sumador_simple_2_cout, sumador_simple_2_s;

  sumador_simple sumador_simple_1 (.A(Cin), .B(sumador_simple_2_s), .S(S), .Cout(sumador_simple_1_cout));
  sumador_simple sumador_simple_2 (.A(A), .B(B), .S(sumador_simple_2_s), .Cout(sumador_simple_2_cout));
  or or_1 (Cout, sumador_simple_1_cout, sumador_simple_2_cout);
endmodule

module sumador_4 (
  input  Cin,
  input  [3:0] A,
  input  [3:0] B,
  output [3:0] S,
  output Cout
);

  wire sumador_completo_1_cout, sumador_completo_2_cout, sumador_completo_3_cout;

  sumador_completo sumador_completo_1 (.Cin(Cin), .A(A[0]), .B(B[0]), .S(S[0]), .Cout(sumador_completo_1_cout));
  sumador_completo sumador_completo_2 (
    .Cin(sumador_completo_1_cout), .A(A[1]), .B(B[1]), .S(S[1]), .Cout(sumador_completo_2_cout));
  sumador_completo sumador_completo_3 (
    .Cin(sumador_completo_2_cout), .A(A[2]), .B(B[2]), .S(S[2]), .Cout(sumador_completo_3_cout));
  sumador_completo sumador_completo_4 (.Cin(sumador_completo_3_cout), .A(A[3]), .B(B[3]), .S(S[3]), .Cout(Cout));
  Hex_Digit_Display hex_digit_display_1 (.value(S));  // open: dp
endmodule

module comparador_cero (
  input  [3:0] A,
  output Z
);

  wire not_1_out, not_2_out, or_1_out, or_2_out;

  or or_1 (or_1_out, A[0], A[1]);
  or or_2 (or_2_out, A[2], A[3]);
  not not_1 (not_1_out, or_1_out);
  not not_2 (not_2_out, or_2_out);
  and and_1 (Z, not_1_out, not_2_out);
endmodule

module sumador_flags (
  input  Cin,
  input  [3:0] A,
  input  [3:0] B,
  output [3:0] S,
  output Z,
  output N,
  output C,
  output V
);

  wire not_1_out, sumador_completo_1_cout, sumador_completo_2_cout, sumador_completo_3_cout, xor_1_out,
       xor_2_out;

  sumador_completo sumador_completo_1 (.Cin(Cin), .A(A[0]), .B(B[0]), .S(S[0]), .Cout(sumador_completo_1_cout));
  sumador_completo sumador_completo_2 (
    .Cin(sumador_completo_1_cout), .A(A[1]), .B(B[1]), .S(S[1]), .Cout(sumador_completo_2_cout));
  sumador_completo sumador_completo_3 (
    .Cin(sumador_completo_2_cout), .A(A[2]), .B(B[2]), .S(S[2]), .Cout(sumador_completo_3_cout));
  sumador_completo sumador_completo_4 (.Cin(sumador_completo_3_cout), .A(A[3]), .B(B[3]), .S(N), .Cout(C));
  xor xor_1 (xor_1_out, A[3], B[3]);
  not not_1 (not_1_out, xor_1_out);
  xor xor_2 (xor_2_out, N, A[3]);
  and and_1 (V, xor_2_out, not_1_out);
  Hex_Digit_Display hex_digit_display_1 (.value({N, S[2:0]}));  // open: dp
  comparador_cero comparador_cero_1 (.A({N, S[2:0]}), .Z(Z));

  assign S[3] = N;
endmodule

module incrementador_4 (
  input  [3:0] A,
  output [3:0] S
);

  wire sumador_simple_1_cout, sumador_simple_2_cout, sumador_simple_3_cout;

  sumador_simple sumador_simple_1 (.A(1'b1), .B(A[0]), .S(S[0]), .Cout(sumador_simple_1_cout));
  sumador_simple sumador_simple_2 (.A(sumador_simple_1_cout), .B(A[1]), .S(S[1]), .Cout(sumador_simple_2_cout));
  sumador_simple sumador_simple_3 (.A(sumador_simple_2_cout), .B(A[2]), .S(S[2]), .Cout(sumador_simple_3_cout));
  sumador_simple sumador_simple_4 (.A(sumador_simple_3_cout), .B(A[3]), .S(S[3]));  // open: Cout
  Hex_Digit_Display hex_digit_display_1 (.value(S));  // open: dp
endmodule

module inversor_4 (
  input  [3:0] A,
  input  INV,
  output [3:0] S
);

  wire [3:0] incrementador_4_1_s, not_1_out;

  not not_1 (not_1_out[0], A[0]);
  not not_2 (not_1_out[1], A[1]);
  not not_3 (not_1_out[2], A[2]);
  not not_4 (not_1_out[3], A[3]);
  incrementador_4 incrementador_4_1 (.A(not_1_out), .S(incrementador_4_1_s));
  Multiplexer #(.width(4)) multiplexer_1 (.in0(A), .in1(incrementador_4_1_s), .out(S), .sel(INV));
  Hex_Digit_Display hex_digit_display_1 (.value(S));  // open: dp
endmodule

module ALU (
  input  [3:0] A,
  input  [1:0] OP,
  input  [3:0] B,
  output [3:0] S,
  output Z,
  output N,
  output C,
  output V
);

  wire sumador_flags_2_c;
  wire [3:0] and_1_out, inversor_4_1_s, or_1_out, sumador_flags_1_s, sumador_flags_2_s;
  wire [4:4] comparador_cero_1_z, comparador_cero_2_z;
  wire [7:4] sumador_flags_1_z, sumador_flags_2_z;

  and and_1 (and_1_out[0], A[0], B[0]);
  and and_2 (and_1_out[1], A[1], B[1]);
  sumador_flags sumador_flags_1 (
    .A(A), .B(B), .S(sumador_flags_1_s), .Z(sumador_flags_1_z[4]), .N(sumador_flags_1_z[5]),
    .C(sumador_flags_1_z[6]), .V(sumador_flags_1_z[7]));  // open: Cin
  sumador_flags sumador_flags_2 (
    .A(A), .B(inversor_4_1_s), .S(sumador_flags_2_s), .Z(sumador_flags_2_z[4]), .N(sumador_flags_2_z[5]),
    .C(sumador_flags_2_c), .V(sumador_flags_2_z[7]));  // open: Cin
  inversor_4 inversor_4_1 (.A(B), .INV(1'b1), .S(inversor_4_1_s));
  and and_3 (and_1_out[2], A[2], B[2]);
  or or_1 (or_1_out[0], A[0], B[0]);
  or or_2 (or_1_out[2], A[2], B[2]);
  not not_1 (sumador_flags_2_z[6], sumador_flags_2_c);
  or or_3 (or_1_out[1], A[1], B[1]);
  or or_4 (or_1_out[3], A[3], B[3]);
  and and_4 (and_1_out[3], A[3], B[3]);
  comparador_cero comparador_cero_1 (.A(and_1_out), .Z(comparador_cero_1_z[4]));
  comparador_cero comparador_cero_2 (.A(or_1_out), .Z(comparador_cero_2_z[4]));
  Multiplexer #(.select(2), .width(8)) multiplexer_1 (
    .in0({sumador_flags_1_z, sumador_flags_1_s}), .in1({sumador_flags_2_z, sumador_flags_2_s}),
    .in2({2'b00, and_1_out[3], comparador_cero_1_z[4], and_1_out}),
    .in3({2'b00, or_1_out[3], comparador_cero_2_z[4], or_1_out}), .out({V, C, N, Z, S}), .sel(OP));
  Hex_Digit_Display hex_digit_display_1 (.value(S));  // open: dp
endmodule

module verificador (
  output [3:0] out_1,
  output [3:0] out_2,
  output [1:0] out_3,
  output [3:0] res,
  output halt,
  output Z,
  output N,
  output C,
  output V
);

  wire clock_1_out;

  Clock clock_1 (.out(clock_1_out));
  Counter #(.max('h3ff), .width(10)) counter_1 (
    .clk(clock_1_out), .carry(halt), .Q({out_3, out_2, out_1}));  // open: clr, load, up, count, D
  ALU alu_1 (.A(out_1), .OP(out_3), .B(out_2), .S(res), .Z(Z), .N(N), .C(C), .V(V));
endmodule
